# Fritzing sketch sketch_fritzing (saved by Fritzing 0.9.5d)
circuit board: 8.46667cm x 5.64444cm
breadboards: 1

parts:
  U1 = ESP32-38PinWide [part_number=ESP32-38PinWide]
  Sensor_2 = HC-SR04 Ultrasonic Distance Sensor
  Sensor_1 = HC-SR04 Ultrasonic Distance Sensor
  M1 = ac light dimmer-4terminal
  R1 = Photocell (LDR) [package=THT]
  220R = Resistor [tolerance=±5% resistance=220 package="2010 [SMD]"]
  LED = LEDs [package=led10mm]
  Part1 = Current Sensor 5A
  V1 = AC Power [voltage=5 frequency=60]

nets (from the schematic view):
  N1: U1.GPIO34, M1.LOAD1, Part1.2, Part1.OUT
  N2: U1.GPIO35, R1.pin_0, 220R.Pin_1
  N3: U1.GPIO12, Sensor_1.GND
  N4: U1.GPIO13, Sensor_1.TRIG
  VCC: U1.VIN, Sensor_1.VCC, R1.pin_1, Part1.VCC
  N5: U1.GPIO16, Sensor_2.GND
  N6: U1.GPIO17, Sensor_2.TRIG
  N7: U1.GPIO5, M1.Z-C
  N8: U1.GPIO23, M1.PWM
  VCC_2: Sensor_2.VCC, M1.VCC
  N9: Sensor_2.ECHO, M1.GND
  N10: Sensor_1.ECHO, 220R.Pin_0, Part1.GND
  N11: M1.LOAD2, LED.A
  N12: M1.AC-IN1, V1.V+
  N13: M1.AC-IN2, V1.V-
  N14: LED.C, Part1.1

custom parts:
  ESP32-38PinWide: Generic 38-Pin ESP32 with wide format (only access to one side of pins on a breadboard) based on Stephen Lilley's HiLetgo ESP-WROOM-32 ESP32 ESP-32S Development Board.
  ac light dimmer-4terminal: ac light dimmer module 4terminal.
  LEDs: LEDs Standard schematic elements and footprints for 5mm, 3mm, 1206, and 0603 sized LEDs. 5mm - Spark Fun Electronics SKU : COM-00529 (and others)
